// Logisim project ALU.circ as structural Verilog: 1 circuit, main circuit main
module main (
  input  [31:0] A,
  input  [31:0] B,
  input  [4:0] Shift,
  input  CarryIn,
  input  [3:0] Codop
);

  wire and_1_out, and_2_out;
  wire [31:0] adder_1_out, and_3_out, and_4_out, and_5_out, multiplier_1_out, negator_1_out, not_1_out,
       or_1_out, shifter_1_out, shifter_2_out, shifter_3_out, shifter_4_out, subtractor_1_out, xor_1_out;

  and and_1 (and_1_out, CarryIn, Codop[2]);
  and and_2 (and_2_out, CarryIn, ~Codop[2]);  // AND_Gate
  assign and_3_out = A & B;  // AND_Gate and_3, 32 bits wide
  assign xor_1_out = A ^ A;  // XOR_Gate xor_1, 32 bits wide
  Shifter #(.width(32)) shifter_1 (.in(B), .\dist (Shift), .out(shifter_1_out));
  Shifter #(.shift("lr"), .width(32)) shifter_2 (.in(B), .\dist (Shift), .out(shifter_2_out));
  Shifter #(.shift("ar"), .width(32)) shifter_3 (.in(B), .\dist (Shift), .out(shifter_3_out));
  Adder #(.width(32)) adder_1 (.a(A), .b(B), .out(adder_1_out), .cin(and_1_out));  // open: cout
  Subtractor #(.width(32)) subtractor_1 (.a(B), .b(A), .out(subtractor_1_out), .bin(and_2_out));  // open: bout
  Shifter #(.shift("rr"), .width(32)) shifter_4 (.in(B), .\dist (Shift), .out(shifter_4_out));
  assign and_4_out = A & B;  // AND_Gate and_4, 32 bits wide
  Negator #(.width(32)) negator_1 (.in(A), .out(negator_1_out));
  assign or_1_out = A | A;  // OR_Gate or_1, 32 bits wide
  Multiplier #(.width(32)) multiplier_1 (.a(A), .b(A), .out(multiplier_1_out), .cin({32{1'b0}}));  // open: cout
  assign and_5_out = ~A & B;  // AND_Gate and_5, 32 bits wide
  assign not_1_out = ~A;  // NOT_Gate not_1, 32 bits wide
  Multiplexer #(.select(4), .width(32)) multiplexer_1 (
    .in0(and_3_out), .in1(xor_1_out), .in2(shifter_1_out), .in3(shifter_2_out), .in4(shifter_3_out),
    .in5(adder_1_out), .in6(subtractor_1_out), .in7(shifter_4_out), .in8(and_4_out), .in9(negator_1_out),
    .in10(or_1_out), .in11(adder_1_out), .in12(subtractor_1_out), .in13(multiplier_1_out), .in14(and_5_out),
    .in15(not_1_out));  // open: out, sel

  // Other names for the same wires on the sheet: CD[3:0] = Codop; CI = CarryIn; S[4:0] = Shift
endmodule
