// Logisim project ALU_2.circ as structural Verilog: 1 circuit, main circuit main
module main (
  input  [31:0] B,
  input  [31:0] A,
  input  [3:0] Codop,
  input  [4:0] Shift,
  input  CarryIn,
  output [31:0] S,
  output [3:0] Flags
);

  wire and_4_out, C3, C4, C5, C6, C7, C8, C10, C11, C12, or_2_out, subtractor_1_out;
  wire [31:0] adder_1_out, adder_2_out, and_1_out, and_2_out, and_3_out, multiplexer_1_out, multiplier_1_out,
       not_1_out, not_2_out, or_1_out, shifter_1_out, shifter_2_out, shifter_3_out, shifter_4_out,
       subtractor_2_out, subtractor_3_out, subtractor_4_out, xor_1_out;

  BitSelector #(.width(32)) bitselector_1 (.in(B), .out(C3), .sel(Shift));
  BitSelector #(.width(32)) bitselector_2 (.in(B), .out(C4), .sel(Shift));
  BitSelector #(.width(32)) bitselector_3 (.in(B), .out(C5), .sel(Shift));
  BitSelector #(.width(32)) bitselector_4 (.in(B), .out(C8), .sel(Shift));
  Subtractor #(.width(1)) subtractor_1 (.a(CarryIn), .b(1'b1), .out(subtractor_1_out));  // open: bin, bout
  assign and_1_out = A & B;  // AND_Gate and_1, 32 bits wide
  assign xor_1_out = A ^ B;  // XOR_Gate xor_1, 32 bits wide
  Shifter #(.width(32)) shifter_1 (.in(B), .\dist (Shift), .out(shifter_1_out));
  Shifter #(.shift("lr"), .width(32)) shifter_2 (.in(B), .\dist (Shift), .out(shifter_2_out));
  Shifter #(.shift("ar"), .width(32)) shifter_3 (.in(B), .\dist (Shift), .out(shifter_3_out));
  Adder #(.width(32)) adder_1 (.a(B), .b(A), .out(adder_1_out), .cin(CarryIn), .cout(C6));
  Subtractor #(.width(32)) subtractor_2 (.a(B), .b(A), .out(subtractor_2_out), .bin(subtractor_1_out), .bout(C7));
  Shifter #(.shift("rr"), .width(32)) shifter_4 (.in(B), .\dist (Shift), .out(shifter_4_out));
  assign and_2_out = A & B;  // AND_Gate and_2, 32 bits wide
  Subtractor #(.width(32)) subtractor_3 (.a({32{1'b0}}), .b(A), .out(subtractor_3_out), .bout(C10));  // open: bin
  Subtractor #(.width(32)) subtractor_4 (.a(B), .b(A), .out(subtractor_4_out), .bout(C11));  // open: bin
  Adder #(.width(32)) adder_2 (.a(A), .b(B), .out(adder_2_out), .cout(C12));  // open: cin
  assign or_1_out = A | B;  // OR_Gate or_1, 32 bits wide
  Multiplier #(.width(32)) multiplier_1 (.a(A), .b(B), .out(multiplier_1_out));  // open: cin, cout
  assign and_3_out = B & not_1_out;  // AND_Gate and_3, 32 bits wide
  assign not_1_out = ~A;  // NOT_Gate not_1, 32 bits wide
  assign not_2_out = ~A;  // NOT_Gate not_2, 32 bits wide
  Multiplexer #(.select(4), .width(32)) multiplexer_1 (
    .in0(and_1_out), .in1(xor_1_out), .in2(shifter_1_out), .in3(shifter_2_out), .in4(shifter_3_out),
    .in5(adder_1_out), .in6(subtractor_2_out), .in7(shifter_4_out), .in8(and_2_out), .in9(subtractor_3_out),
    .in10(subtractor_4_out), .in11(adder_2_out), .in12(or_1_out), .in13(multiplier_1_out), .in14(and_3_out),
    .in15(not_2_out), .out(multiplexer_1_out), .sel(Codop));
  // Probe on multiplexer_1_out
  or or_2 (or_2_out, ~Codop[0], Codop[1]);  // OR_Gate
  and and_4 (and_4_out, or_2_out, ~Codop[2], Codop[3]);  // AND_Gate
  Multiplexer #(.width(32)) multiplexer_2 (.in0(B), .in1(multiplexer_1_out), .out(S), .sel(and_4_out));
endmodule
