// Logisim project Ctl_Data_Processing.circ as structural Verilog: 1 circuit, main circuit Data_Processing
module Data_Processing (
  input  Enable,
  input  [15:0] Instruction,
  output [2:0] Rd,
  output [2:0] Rn,
  output [2:0] Rm,
  output [3:0] ALU_Opcode,
  output [3:0] Flags_Update_Mask
);

  wire [1:0] multiplexer_1_out;

  Multiplexer #(.select(4)) multiplexer_1 (
    .in0(1'b0), .in1(1'b0), .in2(1'b0), .in3(1'b0), .in4(1'b0), .in5(1'b1), .in6(1'b1), .in7(1'b0),
    .in8(1'b0), .in9(1'b1), .in10(1'b1), .in11(1'b1), .in12(1'b0), .in13(1'b0), .in14(1'b0), .in15(1'b0),
    .out(multiplexer_1_out[0]), .sel(Instruction[9:6]));
  not not_1 (multiplexer_1_out[1], Instruction[8]);
  assign Rd = Enable ? Instruction[2:0] : 3'bz;  // Controlled_Buffer controlled_buffer_1
  assign Rn = Enable ? Instruction[2:0] : 3'bz;  // Controlled_Buffer controlled_buffer_2
  assign Rm = Enable ? Instruction[5:3] : 3'bz;  // Controlled_Buffer controlled_buffer_3
  assign ALU_Opcode = Enable ? Instruction[9:6] : 4'bz;  // Controlled_Buffer controlled_buffer_4
  assign Flags_Update_Mask = Enable ? {2'b11, multiplexer_1_out} : 4'bz;  // Controlled_Buffer controlled_buffer_5
  Pull_Resistor pull_resistor_1 (.node(Rd));
  Pull_Resistor pull_resistor_2 (.node(Rn));
  Pull_Resistor pull_resistor_3 (.node(Rm));
  Pull_Resistor pull_resistor_4 (.node(ALU_Opcode));
  Pull_Resistor pull_resistor_5 (.node(Flags_Update_Mask));

  // Notes on the sheet:
  //   Note 2: RSB instruction has Rn as 1st operand.
  //   MUL instruction has Rn as 1st operand and Rdm as 2nd operand
  //   For simplification purposes, Rm is used for 1st operand both here and in the ALU.
  //   Note: instructions that does not save the result will still have the second operand as the destination register, the ALU will copy the second register to the destination register
endmodule
