// Logisim project Ctl_Load_Store.circ as structural Verilog: 1 circuit, main circuit Load_Store
module Load_Store (
  input  Enable,
  input  [15:0] Instruction,
  input  Clk,
  input  Reset,
  input  [31:0] Stack_Pointer,
  output Store,
  output Load,
  output PC_Hold,
  output [2:0] Rmd,
  output [31:0] RAM_Addr
);

  wire and_1_out, and_2_out, d_ff_1_q, d_ff_1_qn, or_1_out;
  wire [31:0] adder_1_out, bit_extender_1_out;

  D_Flip_Flop d_ff_1 (.D(and_1_out), .Q(d_ff_1_q), .Qn(d_ff_1_qn), .reset(or_1_out));  // open: clk, preset
  and and_1 (and_1_out, ~d_ff_1_q, Instruction[11]);  // AND_Gate
  or or_1 (or_1_out, ~Instruction[11], Reset, ~Enable);  // OR_Gate
  assign bit_extender_1_out = {{24{Instruction[7]}}, Instruction[7:0]};  // Bit_Extender bit_extender_1
  Adder #(.width(32)) adder_1 (.a(bit_extender_1_out), .b(Stack_Pointer), .out(adder_1_out), .cin(1'b0));  // open: cout
  and and_2 (and_2_out, d_ff_1_qn, Instruction[11]);
  assign Rmd = Enable ? Instruction[10:8] : 3'bz;  // Controlled_Buffer controlled_buffer_1
  assign RAM_Addr = Enable ? adder_1_out : 32'bz;  // Controlled_Buffer controlled_buffer_2
  and and_3 (Store, Instruction[11], Enable);
  and and_4 (Load, d_ff_1_q, Instruction[11], Enable);
  // AND_Gate and_5 has open pins: in0=and_2_out, in1=Enable, out=open
  Pull_Resistor pull_resistor_1 (.node(Rmd));
  Pull_Resistor pull_resistor_2 (.node(RAM_Addr));

  // Notes on the sheet:
  //   Delay load and hold PC for 1 cycle for the RAM to send out requested data 
endmodule
