// Logisim project Ctl_Shift_Add_Sub_Mov.circ as structural Verilog: 5 circuits, main circuit Shift_Add_Sub_Mov
module Shift_Add_Sub_Mov (
  input  Enable,
  input  [15:0] Instruction,
  output [3:0] Flags_Update_Mask,
  output Carry,
  output Imm32_Enable,
  output [2:0] Rm,
  output [2:0] Rn,
  output [2:0] Rd,
  output [4:0] Imm5,
  output [31:0] Imm32,
  output [3:0] ALU_Opcode
);

  wire and_1_out, and_2_out, and_4_out, and_5_out, comparator_1_eq, or_2_out;
  wire [0:0] and_3_out;
  wire [1:0] or_3_out;
  wire [2:0] multiplexer_4_out, multiplexer_5_out;
  wire [3:0] adder_1_out, adder_2_out, multiplexer_3_out, multiplexer_6_out;
  wire [31:0] bit_extender_1_out, bit_extender_2_out, multiplexer_1_out, multiplexer_2_out, negator_1_out;

  and and_1 (and_1_out, Instruction[11], Instruction[12]);
  and and_2 (and_2_out, ~Instruction[11], ~Instruction[12]);  // AND_Gate
  assign bit_extender_1_out = {{24{1'b0}}, Instruction[7:0]};  // Bit_Extender bit_extender_1
  and and_3 (and_3_out[0], and_1_out, Instruction[9]);
  Adder #(.width(4)) adder_1 (.a(4'b0010), .b(Instruction[14:11]), .out(adder_1_out), .cin(1'b0));  // open: cout
  or or_1 (or_3_out[1], Instruction[11], Instruction[12], ~Instruction[13]);  // OR_Gate
  and and_4 (and_4_out, Instruction[10], Instruction[11], Instruction[12]);
  or or_2 (or_2_out, and_4_out, Instruction[13]);
  assign bit_extender_2_out = {{29{1'b0}}, Instruction[8:6]};  // Bit_Extender bit_extender_2
  Multiplexer #(.width(32)) multiplexer_1 (
    .in0(bit_extender_1_out), .in1(negator_1_out), .out(multiplexer_1_out), .sel(and_2_out));
  Negator #(.width(32)) negator_1 (.in(bit_extender_1_out), .out(negator_1_out));
  Adder #(.width(4)) adder_2 (
    .a({3'b000, and_3_out[0]}), .b(adder_1_out), .out(adder_2_out), .cin(1'b0));  // open: cout
  and and_5 (and_5_out, or_3_out[1], Instruction[13]);
  or or_3 (or_3_out[0], and_5_out, and_1_out);
  Multiplexer #(.width(32)) multiplexer_2 (
    .in0(bit_extender_2_out), .in1(multiplexer_1_out), .out(multiplexer_2_out), .sel(Instruction[13]));
  Multiplexer #(.select(2), .width(4)) multiplexer_3 (
    .in0(4'b1001), .in1(4'b1010), .in2(4'b0101), .in3(4'b0110), .out(multiplexer_3_out),
    .sel(Instruction[12:11]));
  Multiplexer #(.width(3)) multiplexer_4 (
    .in0(Instruction[5:3]), .in1(Instruction[10:8]), .out(multiplexer_4_out), .sel(Instruction[13]));
  Multiplexer #(.width(3)) multiplexer_5 (
    .in0(Instruction[2:0]), .in1(Instruction[10:8]), .out(multiplexer_5_out), .sel(Instruction[13]));
  Multiplexer #(.width(4)) multiplexer_6 (
    .in0(adder_2_out), .in1(multiplexer_3_out), .out(multiplexer_6_out), .sel(Instruction[13]));
  Comparator #(.width(4)) comparator_1 (.a(4'b0110), .b(multiplexer_6_out), .eq(comparator_1_eq));  // open: gt, lt
  assign Flags_Update_Mask = Enable ? {2'b11, or_3_out} : 4'bz;  // Controlled_Buffer controlled_buffer_1
  Pull_Resistor pull_resistor_1 (.node(Flags_Update_Mask));
  and and_6 (Carry, Enable, comparator_1_eq);
  and and_7 (Imm32_Enable, Enable, or_2_out);
  Pull_Resistor pull_resistor_2 (.node(Rm));
  assign Rm = Enable ? Instruction[8:6] : 3'bz;  // Controlled_Buffer controlled_buffer_2
  Pull_Resistor pull_resistor_3 (.node(Rn));
  assign Rn = Enable ? multiplexer_4_out : 3'bz;  // Controlled_Buffer controlled_buffer_3
  Pull_Resistor pull_resistor_4 (.node(Rd));
  assign Rd = Enable ? multiplexer_5_out : 3'bz;  // Controlled_Buffer controlled_buffer_4
  Pull_Resistor pull_resistor_5 (.node(Imm5));
  assign Imm5 = Enable ? Instruction[10:6] : 5'bz;  // Controlled_Buffer controlled_buffer_5
  Pull_Resistor pull_resistor_6 (.node(Imm32));
  assign Imm32 = Enable ? multiplexer_2_out : 32'bz;  // Controlled_Buffer controlled_buffer_6
  Pull_Resistor pull_resistor_7 (.node(ALU_Opcode));
  assign ALU_Opcode = Enable ? multiplexer_6_out : 4'bz;  // Controlled_Buffer controlled_buffer_7

  // Notes on the sheet:
  //   ADD, SUB
  //   LSL
  //   Note: ALU uses Rn register for shifts. Use Rn instead of Rm for shifts (immediate) here too
  //   Note 3: Imm32_Enable forces the use of the immediate for Rm register
  //   ADDi, SUBi
  //   Note 2: MOV uses RSB ALU opcode with Imm8 reversed so that it is copied to output register
  //   Pull output low on Enable = 0
  //   !MOV
  //   SUB
  //   only ADD and SUB use Rm
  //   Enable carry for SUB since it is reversed in ALU
  //   ALU will use Imm32 instead of Rm
endmodule

module is_MOVS (
  input  [2:0] InIsMov,
  output isMov
);

  wire not_1_out, not_2_out;

  not not_1 (not_1_out, InIsMov[2]);
  not not_2 (not_2_out, InIsMov[1]);
  and and_1 (isMov, not_1_out, not_2_out, InIsMov[0]);
endmodule

module is_ADD_SUB (
  input  [4:0] inADDSUB,
  output outADDSUB
);

  wire not_1_out, not_2_out, not_3_out;

  not not_1 (not_1_out, inADDSUB[4]);
  not not_2 (not_2_out, inADDSUB[3]);
  not not_3 (not_3_out, inADDSUB[2]);
  and and_1 (outADDSUB, not_1_out, not_2_out, not_3_out, inADDSUB[1], inADDSUB[0]);
endmodule

module is_SHIFT (
  input  [2:0] inSHIFT,
  output outSHIFT
);

  wire not_1_out, not_2_out, not_3_out;

  not not_1 (not_1_out, inSHIFT[2]);
  not not_2 (not_2_out, inSHIFT[1]);
  not not_3 (not_3_out, inSHIFT[0]);
  and and_1 (outSHIFT, not_1_out, not_2_out, not_3_out);
endmodule

module use_IMM3 (
  input  is_ADD_SUB,
  input  is_10thBit,
  output outIsIMM3
);

  and and_1 (outIsIMM3, is_ADD_SUB, is_10thBit);
endmodule
